# Fritzing sketch Robotic Arm V3 (saved by Fritzing 0.9.3b)
breadboards: 1

parts:
  Part1 = Arduino Uno (Rev3) - ICSP
  R1 = Trimmer Potentiometer [maximum_resistance=10kΩ package=THT]
  R2 = Trimmer Potentiometer [maximum_resistance=10kΩ package=THT]
  R3 = Trimmer Potentiometer [maximum_resistance=10kΩ package=THT]
  R4 = Trimmer Potentiometer [maximum_resistance=10kΩ package=THT]
  Record_button = Pushbutton [package="[THT]"]
  Play_button = Pushbutton [package="[THT]"]
  J1 = Basic Servo
  J2 = Basic Servo
  J3 = Basic Servo
  BAT1 = BC9VPC [package=bc9vpc]
  J4 = Basic Servo
  Red_diode = Diode [package=diode-hv]
  Blue_diode = Diode [package=diode-hv]
  R5 = Resistor [tolerance=±5% resistance=10k package="0402 [SMD]"]
  R6 = Resistor [tolerance=±5% resistance=10k package="0402 [SMD]"]

nets:
  N1: Part1.A0, R1.wiper
  N2: Part1.A1, R2.wiper
  N3: Part1.A2, R3.wiper
  N4: Part1.A3, R4.wiper
  N5: Part1.ICSP_MISO, Part1.D12/MISO, R6.Pin_0
  N6: Part1.ICSP_MOSI, Part1.D11_PWM/MOSI, R5.Pin_0
  N7: Part1.GND, R1.leg2, R2.leg2, R3.leg2, R4.leg2, Record_button.Pin_2, Play_button.Pin_1, Play_button.Pin_2, Red_diode.C, Blue_diode.C
  N8: Part1.5V, R1.leg1, R2.leg1, R3.leg1, R4.leg1
  N9: Part1.D8, J2.pulse
  N10: Part1.D9_PWM, J3.pulse
  N11: Part1.D3_PWM, J4.pulse
  N12: Part1.D5_PWM, Play_button.Pin_4
  N13: Part1.D6_PWM, Record_button.Pin_4
  N14: Part1.D7, J1.pulse
  GND: J1.gnd, J2.gnd, J3.gnd, BAT1.V-, J4.gnd
  VCC: J1.vcc, J2.vcc, J3.vcc, BAT1.V+, J4.vcc
  N15: Red_diode.A, R5.Pin_1
  N16: Blue_diode.A, R6.Pin_1
